// Logisim project projetoSistemasDigitais.circ as structural Verilog: 11 circuits, main circuit main
module main (
  output [8:0] out_1
);

  wire _0_5_out, _1_out, fsm_moore_1_saida, latchrs_1_q, not_1_out, or_1_out;
  wire [3:0] C1, C1_2;

  or or_1 (or_1_out, _0_5_out, _1_out);
  Button _0_5 (.out(_0_5_out));
  Button _1 (.out(_1_out));
  not not_1 (not_1_out, fsm_moore_1_saida);
  FSM_Moore fsm_moore_1 (.CLOCK(or_1_out), .ENTRADA(latchrs_1_q), .SAIDA(fsm_moore_1_saida));
  latchRS latchrs_1 (.R(_1_out), .C(or_1_out), .Q(latchrs_1_q));  // open: Q_prime
  contador_assinc_decada contador_assinc_decada_1 (
    .CLOCK(not_1_out), .s0(C1[0]), .s1(C1[1]), .s2(C1[2]), .s3(C1[3]), .s4(C1_2[0]), .s5(C1_2[1]),
    .s6(C1_2[2]), .s7(C1_2[3]));
  contador_moeda contador_moeda_1 (._50C(_0_5_out), ._1R(_1_out), .saida(out_1));
  Hex_Digit_Display hex_digit_display_1 (.value(C1_2));  // open: dp
  Hex_Digit_Display hex_digit_display_2 (.value(C1));  // open: dp
endmodule

module circuito_Moore (
  input  Q0,
  input  Q1,
  input  E,
  output D0,
  output D1,
  output S
);

  wire and_1_out, and_2_out, and_3_out, and_4_out, and_5_out, and_6_out, not_1_out, not_2_out, not_3_out,
       not_4_out, not_5_out, not_6_out, not_7_out;

  not not_1 (not_1_out, Q0);
  not not_2 (not_2_out, E);
  not not_3 (not_3_out, Q0);
  not not_4 (not_4_out, Q1);
  not not_5 (not_5_out, E);
  not not_6 (not_6_out, Q1);
  not not_7 (not_7_out, Q0);
  and and_1 (and_1_out, not_1_out, not_2_out);
  and and_2 (and_2_out, not_3_out, Q1);
  and and_3 (and_3_out, Q0, not_4_out, E);
  and and_4 (and_4_out, Q0, Q1, not_5_out);
  and and_5 (and_5_out, Q0, not_6_out);
  and and_6 (and_6_out, not_7_out, Q1);
  and and_7 (S, Q0, Q1);
  or u_D0 (D0, and_1_out, and_2_out, and_3_out, and_4_out);
  or u_D1 (D1, E, and_5_out, and_6_out);
endmodule

module FSM_Moore (
  input  CLOCK,
  input  ENTRADA,
  output SAIDA
);

  wire Circuito_d0, Circuito_d1, D0_q, D1_q;

  D_Flip_Flop D1 (.clk(CLOCK), .D(Circuito_d1), .Q(D1_q));  // open: Qn, preset, en, reset
  circuito_Moore Circuito (.Q0(D0_q), .Q1(D1_q), .E(ENTRADA), .D0(Circuito_d0), .D1(Circuito_d1), .S(SAIDA));
  D_Flip_Flop D0 (.clk(CLOCK), .D(Circuito_d0), .Q(D0_q));  // open: Qn, preset, en, reset

  // Other names for the same wires on the sheet: ck = CLOCK; E = ENTRADA; S = SAIDA
endmodule

module contador_moeda (
  input  _50C,
  input  _1R,
  output [8:0] saida
);

  wire and_1_out, contador_1bit_1_out, or_1_out;

  contador_1BIT contador_1bit_1 (.CLOCK(_50C), .s0(saida[0]), .OUT(contador_1bit_1_out));
  and and_1 (and_1_out, _50C, contador_1bit_1_out);
  or or_1 (or_1_out, _1R, and_1_out);
  contador_assinc_decada contador_assinc_decada_1 (
    .CLOCK(or_1_out), .s0(saida[1]), .s1(saida[2]), .s2(saida[3]), .s3(saida[4]), .s4(saida[5]),
    .s5(saida[6]), .s6(saida[7]), .s7(saida[8]));

  // Other names for the same wires on the sheet: _1REAL = _1R; _50CENTAVOS = _50C; LSB = saida[0]
endmodule

module somador9bits (
  input  LSB_A,
  input  LSB_B,
  input  [7:0] A_8BITS,
  input  [7:0] B_8BITS,
  output [9:0] SAIDA_10BITS
);

  wire O0;

  somador8bits somador8bits_1 (
    .A7(A_8BITS[7]), .B7(B_8BITS[7]), .A6(A_8BITS[6]), .B6(B_8BITS[6]), .A5(A_8BITS[5]), .B5(B_8BITS[5]),
    .A4(A_8BITS[4]), .B4(B_8BITS[4]), .A3(A_8BITS[3]), .B3(B_8BITS[3]), .A2(A_8BITS[2]), .B2(B_8BITS[2]),
    .A1(A_8BITS[1]), .B1(B_8BITS[1]), .A0(A_8BITS[0]), .B0(B_8BITS[0]), .CIN0(O0),
    .SAIDAS4_8(SAIDA_10BITS[9:5]), .SAIDAS0_3(SAIDA_10BITS[4:1]));
  Ha ha_1 (.A(LSB_B), .B(LSB_A), .Cout(O0), .S(SAIDA_10BITS[0]));

  // Other names for the same wires on the sheet: A0 = A_8BITS[0]; A1 = A_8BITS[1]; A2 = A_8BITS[2]; A3 = A_8BITS[3];
  //   A4 = A_8BITS[4]; A5 = A_8BITS[5]; A6 = A_8BITS[6]; A7 = A_8BITS[7]; B0 = B_8BITS[0]; B1 = B_8BITS[1];
  //   B2 = B_8BITS[2]; B3 = B_8BITS[3]; B4 = B_8BITS[4]; B5 = B_8BITS[5]; B6 = B_8BITS[6]; B7 = B_8BITS[7];
  //   S0 = SAIDA_10BITS[0]; SAIDA[9:0] = SAIDA_10BITS
endmodule

module somador4bits (
  input  A3,
  input  A2,
  input  A1,
  input  A0,
  input  B3,
  input  B2,
  input  B1,
  input  B0,
  input  CIN0,
  output S4,
  output S3,
  output S2,
  output S1,
  output S0
);

  wire O0, O1, O2;

  FA fa_1 (.A(A3), .B(B3), .Cin(O2), .Cout(S4), .S(S3));
  FA fa_2 (.A(A2), .B(B2), .Cin(O1), .Cout(O2), .S(S2));
  FA fa_3 (.A(A0), .B(B0), .Cin(CIN0), .Cout(O0), .S(S0));
  FA fa_4 (.A(A1), .B(B1), .Cin(O0), .Cout(O1), .S(S1));
endmodule

module somador8bits (
  input  A7,
  input  A6,
  input  A5,
  input  A4,
  input  A3,
  input  A2,
  input  A1,
  input  A0,
  input  B7,
  input  B6,
  input  B5,
  input  B4,
  input  B3,
  input  B2,
  input  B1,
  input  B0,
  input  CIN0,
  output [4:0] SAIDAS4_8,
  output [3:0] SAIDAS0_3
);

  wire O4;

  somador4bits somador4bits_1 (
    .A3(A7), .B3(B7), .A2(A6), .B2(B6), .A1(A5), .B1(B5), .A0(A4), .B0(B4), .S4(SAIDAS4_8[4]),
    .S3(SAIDAS4_8[3]), .S2(SAIDAS4_8[2]), .S1(SAIDAS4_8[1]), .S0(SAIDAS4_8[0]), .CIN0(O4));
  somador4bits somador4bits_2 (
    .A3(A3), .B3(B3), .A2(A2), .B2(B2), .A1(A1), .B1(B1), .A0(A0), .B0(B0), .S4(O4), .S3(SAIDAS0_3[3]),
    .S2(SAIDAS0_3[2]), .S1(SAIDAS0_3[1]), .S0(SAIDAS0_3[0]), .CIN0(CIN0));
endmodule

module contador_1BIT (
  input  CLOCK,
  output s0,
  output OUT
);

  wire not_1_out;

  not not_1 (not_1_out, CLOCK);
  J_K_Flip_Flop j_k_ff_1 (.J(1'b1), .clk(not_1_out), .K(1'b1), .Q(OUT), .en(1'b1));  // open: Qn, preset, reset

  assign s0 = OUT;
endmodule

module Circuito_Maeley (
  input  Q0,
  input  Q1,
  input  E,
  output D0,
  output D1,
  output S
);

  wire and_1_out, and_2_out, and_3_out, and_4_out, and_5_out, and_6_out, and_7_out, and_8_out, not_1_out,
       not_2_out, not_3_out, not_4_out, not_5_out, not_6_out, not_7_out, not_8_out, not_9_out;

  not not_1 (not_1_out, Q0);
  not not_2 (not_2_out, E);
  not not_3 (not_3_out, Q0);
  not not_4 (not_4_out, Q1);
  not not_5 (not_5_out, E);
  not not_6 (not_6_out, Q1);
  not not_7 (not_7_out, Q0);
  not not_8 (not_8_out, Q0);
  and and_1 (and_1_out, not_1_out, not_2_out);
  and and_2 (and_2_out, not_3_out, Q1);
  and and_3 (and_3_out, Q0, not_4_out, E);
  and and_4 (and_4_out, Q0, Q1, not_5_out);
  and and_5 (and_5_out, Q0, not_6_out);
  and and_6 (and_6_out, not_7_out, Q1);
  not not_9 (not_9_out, Q1);
  and and_7 (and_7_out, not_9_out, Q0);
  and and_8 (and_8_out, Q1, not_8_out, E);
  or u_D0 (D0, and_1_out, and_2_out, and_3_out, and_4_out);
  or u_D1 (D1, E, and_5_out, and_6_out);
  or u_S (S, and_7_out, and_8_out);
endmodule

module TESTE (
  output [8:0] out_1
);

  wire _0_5_out, _1_out, fsm_maeley_1_saida, not_1_out, or_1_out;
  wire [3:0] C1, C1_2;

  or or_1 (or_1_out, _0_5_out, _1_out);
  Button _0_5 (.out(_0_5_out));
  Button _1 (.out(_1_out));
  not not_1 (not_1_out, fsm_maeley_1_saida);
  FSM_Maeley fsm_maeley_1 (.CLOCK(or_1_out), .ENTRADA(or_1_out), .SAIDA(fsm_maeley_1_saida));
  S_R_Flip_Flop s_r_ff_1 (.S(_1_out), .clk(or_1_out), .R(_0_5_out), .Q(or_1_out));  // open: Qn, preset, reset, en
  contador_moeda contador_moeda_1 (._50C(_0_5_out), ._1R(_1_out), .saida(out_1));
  contador_assinc_decada contador_assinc_decada_1 (
    .CLOCK(not_1_out), .s0(C1[0]), .s1(C1[1]), .s2(C1[2]), .s3(C1[3]), .s4(C1_2[0]), .s5(C1_2[1]),
    .s6(C1_2[2]), .s7(C1_2[3]));
  Hex_Digit_Display hex_digit_display_1 (.value(C1));  // open: dp
  Hex_Digit_Display hex_digit_display_2 (.value(C1_2));  // open: dp
endmodule

module FSM_Maeley (
  input  CLOCK,
  input  ENTRADA,
  output SAIDA
);

  wire circuito_maeley_1_d0, circuito_maeley_1_d1, D0_q, D1_q;

  D_Flip_Flop D1 (.clk(CLOCK), .D(circuito_maeley_1_d1), .Q(D1_q));  // open: Qn, preset, en, reset
  Circuito_Maeley circuito_maeley_1 (
    .Q0(D0_q), .Q1(D1_q), .E(ENTRADA), .D0(circuito_maeley_1_d0), .D1(circuito_maeley_1_d1), .S(SAIDA));
  D_Flip_Flop D0 (.clk(CLOCK), .D(circuito_maeley_1_d0), .Q(D0_q));  // open: Qn, preset, en, reset

  // Other names for the same wires on the sheet: ck = CLOCK; E = ENTRADA; S = SAIDA
endmodule
